// Logisim project ExpansionPort.circ as structural Verilog: 1 circuit, main circuit main
module main (
  input  Ax,
  input  nRD,
  input  nWR,
  input  MEM__IO,
  input  nINTA,
  input  nINT,
  output LCDE,
  output nIORQ,
  output nM1,
  output INTR
);

  wire and_1_out, and_2_out, not_1_out, not_3_out, or_1_out;

  not not_1 (not_1_out, MEM__IO);
  not not_2 (INTR, nINT);
  and and_1 (and_1_out, Ax, MEM__IO);
  and and_2 (and_2_out, nRD, nWR);
  not not_3 (not_3_out, and_2_out);
  or or_1 (or_1_out, and_2_out, not_1_out);
  and and_3 (LCDE, and_1_out, not_3_out);
  and and_4 (nIORQ, or_1_out, nINTA);

  assign nM1 = nINTA;

  // Notes on the sheet:
  //   8085
  //   EXP
endmodule
