// Logisim project A64CPM.circ as structural Verilog: 1 circuit, main circuit main
module main (
  input  nMEMRQ,
  input  A15,
  input  nWR,
  input  nM1,
  input  Ax,
  input  nIORQ,
  input  D0,
  input  nRD,
  input  in_9,
  output out_10,
  output out_11,
  output out_12,
  output out_13
);

  wire d_ff_1_qn, not_1_out, not_2_out, or_1_out, or_3_out;

  not not_1 (not_1_out, nM1);
  or or_1 (or_1_out, Ax, nIORQ);
  or or_2 (out_10, nMEMRQ, A15);
  or or_3 (or_3_out, not_1_out, or_1_out);
  not not_2 (not_2_out, or_3_out);
  D_Flip_Flop d_ff_1 (.clk(not_2_out), .D(D0), .Q(out_12), .Qn(d_ff_1_qn), .reset(in_9));  // open: preset
  or or_4 (out_13, d_ff_1_qn, nRD);

  assign out_11 = nWR;

  // Notes on the sheet:
  //   #RESET
  //   #LOWRAMENABLE
  //   #LOWRAMWRITE
  //   ROMSUPRESS
  //   #LOWRAMREAD
endmodule
