// Logisim project A64memoryDecoding.circ as structural Verilog: 1 circuit, main circuit main
module main (
  input  A15,
  input  MEMRQ,
  input  A15_2,
  input  MEMRQ2,
  input  VRAM,
  output ROMSEL,
  output RAMSEL,
  output RAMSEL2,
  output ROMSEL2
);

  wire decoder_1_out1, nand_1_out, nand_2_out;

  Decoder decoder_1 (.out0(RAMSEL2), .out1(decoder_1_out1), .sel(MEMRQ2), .en(A15_2));
  assign ROMSEL2 = VRAM ? decoder_1_out1 : 1'bz;  // Controlled_Buffer controlled_buffer_1
  nand nand_1 (nand_1_out, A15, A15);
  nand nand_2 (nand_2_out, MEMRQ, MEMRQ);
  Pull_Resistor #(.pull(1)) pull_resistor_1 (.node(ROMSEL2));
  nand nand_3 (ROMSEL, nand_1_out, nand_2_out);
  nand nand_4 (RAMSEL, nand_2_out, A15);
endmodule
