// Logisim project Aniol64keyboard.circ as structural Verilog: 1 circuit, main circuit main
module main (
  input  in_1,
  input  IEI,
  input  RESET,
  input  RD,
  input  M1,
  input  IORQ,
  input  D7,
  input  IORQ_2,
  input  A6,
  input  WR,
  output IEO,
  output [6:0] D6_D0,
  output INT
);

  wire and_1_out, and_2_out, and_4_out, clock_1_out, d_ff_1_q, d_ff_2_q, d_ff_2_qn, multiplexer_1_out,
       not_1_out, not_2_out, not_3_out, not_4_out, not_5_out, not_6_out, or_1_out, or_2_out, or_3_out,
       or_4_out, switch_3_p1, switch_3_p2;
  wire [4:0] counter_1_q;
  wire [6:0] register_1_q;
  wire [6:5] pull_resistor_1_node;

  Clock clock_1 (.out(clock_1_out));
  or or_1 (or_1_out, IORQ, A6);
  Counter #(.max('h1f), .width(5)) counter_1 (
    .clr(in_1), .clk(and_1_out), .Q(counter_1_q));  // open: load, up, count, D, carry
  and and_1 (and_1_out, clock_1_out, not_2_out);
  Pull_Resistor pull_resistor_1 (.node(pull_resistor_1_node[5]));
  // Switch switch_1: pin names not known; wires that end beside it: 1'b1, pull_resistor_1_node[5]
  Pull_Resistor pull_resistor_2 (.node(pull_resistor_1_node[6]));
  // Switch switch_2: pin names not known; wires that end beside it: 1'b1, pull_resistor_1_node[6]
  or or_2 (or_2_out, RD, or_1_out);
  or or_3 (or_3_out, or_1_out, WR);
  Register #(.width(7)) register_1 (
    .D({pull_resistor_1_node, counter_1_q}), .clk(multiplexer_1_out), .Q(register_1_q));  // open: en, clr
  not not_1 (not_1_out, or_3_out);
  not not_2 (not_2_out, multiplexer_1_out);
  Pull_Resistor pull_resistor_3 (.node(D6_D0));
  assign D6_D0 = not_3_out ? register_1_q : 7'bz;  // Controlled_Buffer controlled_buffer_1
  not not_3 (not_3_out, or_2_out);
  D_Flip_Flop d_ff_1 (.D(D7), .clk(not_1_out), .Q(d_ff_1_q));  // open: Qn, preset, reset
  Multiplexer #(.enable("false"), .select(2)) multiplexer_1 (
    .in1(switch_3_p2), .out(multiplexer_1_out), .sel(counter_1_q[4:3]));  // open: in0, in2, in3
  LED led_1 (.in(multiplexer_1_out));
  Pull_Resistor pull_resistor_4 (.node(multiplexer_1_out));
  not not_4 (not_4_out, multiplexer_1_out);
  // Switch switch_3: pin names not known; wires that end beside it: switch_3_p1, switch_3_p2
  not not_5 (not_5_out, not_4_out);
  // Buzzer buzzer_1: pin names not known; wires that end beside it: d_ff_1_q
  Demultiplexer #(.enable("false"), .select(3)) demultiplexer_1 (
    .out1(switch_3_p1), .in(1'b1), .sel(counter_1_q[2:0]));  // open: out0, out2, out3, out4, out5, out6, out7
  D_Flip_Flop d_ff_2 (.D(1'b1), .clk(not_5_out), .Q(d_ff_2_q), .Qn(d_ff_2_qn), .reset(not_6_out));  // open: preset
  not not_6 (not_6_out, and_2_out);
  and and_2 (and_2_out, or_4_out, RESET);
  or or_4 (or_4_out, M1, IORQ_2);
  and and_3 (IEO, d_ff_2_qn, IEI);
  and and_4 (and_4_out, IEI, d_ff_2_q);
  not not_7 (INT, and_4_out);

  // Notes on the sheet:
  //   Clock Enable
  //   ALT
  //   SHIFT
  //   Q'
  //   Register OE'
  //   Q
  //   Schmitt triggers and RC network for debouncing
  //   Interrupt Acknowledge
endmodule
