// Logisim project soundCardInterrupts.circ as structural Verilog: 1 circuit, main circuit main
module main (
  input  IEI,
  input  IORQ,
  input  M1,
  output INT,
  output IEO,
  output [7:0] out_6
);

  wire CLK, d_ff_2_qn, not_1_out, not_2_out, or_1_out, or_2_out;
  wire [3:0] counter_1_q;
  wire [7:0] pull_resistor_1_node;

  Clock clock_1 (.out(CLK));
  Counter #(.max('hf), .width(4)) counter_1 (.clk(CLK), .Q(counter_1_q));  // open: clr, load, up, count, D, carry
  not not_1 (not_1_out, counter_1_q[3]);
  D_Flip_Flop d_ff_1 (.D(1'b1), .clk(not_1_out), .Qn(INT), .reset(d_ff_2_qn));  // open: Q, preset
  D_Flip_Flop d_ff_2 (.D(or_2_out), .clk(CLK), .Qn(d_ff_2_qn));  // open: Q, preset, reset
  and and_1 (IEO, INT, IEI);
  or or_1 (or_1_out, IORQ, M1);
  or or_2 (or_2_out, INT, or_1_out);
  not not_2 (not_2_out, or_2_out);
  Pull_Resistor pull_resistor_1 (.node(pull_resistor_1_node[0]));
  Pull_Resistor pull_resistor_2 (.node(pull_resistor_1_node[1]));
  Pull_Resistor pull_resistor_3 (.node(pull_resistor_1_node[2]));
  Pull_Resistor #(.pull(1)) pull_resistor_4 (.node(pull_resistor_1_node[3]));
  Pull_Resistor pull_resistor_5 (.node(pull_resistor_1_node[4]));
  Pull_Resistor pull_resistor_6 (.node(pull_resistor_1_node[5]));
  Pull_Resistor pull_resistor_7 (.node(pull_resistor_1_node[6]));
  Pull_Resistor pull_resistor_8 (.node(pull_resistor_1_node[7]));
  assign out_6 = not_2_out ? pull_resistor_1_node : 8'bz;  // Controlled_Buffer controlled_buffer_1

  // Notes on the sheet:
  //   D0-D7
endmodule
