// Logisim project ProgrammableCounter.circ as structural Verilog: 1 circuit, main circuit main
module main (
  input  IEI,
  input  M1,
  input  IORQ,
  input  RESET,
  input  [7:0] D0_D7,
  input  Ax,
  input  WR,
  input  A0,
  input  A1,
  output INT,
  output IEO,
  output [7:0] out_12,
  output [7:0] To_freq__divider
);

  wire and_1_out, and_2_out, clock_1_out, d_ff_1_q, d_ff_1_qn, not_1_out, not_2_out, not_3_out, not_4_out,
       not_5_out, or_1_out, or_2_out, or_3_out, or_4_out, or_5_out, or_6_out, or_7_out;
  wire [7:0] counter_1_q, register_2_q;

  Counter counter_1 (.clk(clock_1_out), .Q(counter_1_q));  // open: clr, load, up, count, D, carry
  Clock clock_1 (.out(clock_1_out));
  or or_1 (or_1_out, or_6_out, or_7_out);
  Register register_1 (.D(D0_D7), .clk(not_1_out), .Q(To_freq__divider));  // open: en, clr
  not not_1 (not_1_out, or_2_out);
  D_Flip_Flop d_ff_1 (.D(1'b1), .clk(not_2_out), .Q(d_ff_1_q), .Qn(d_ff_1_qn), .reset(not_3_out));  // open: preset
  not not_2 (not_2_out, counter_1_q[7]);
  not not_3 (not_3_out, and_1_out);
  and and_1 (and_1_out, RESET, or_4_out);
  Register register_2 (.D(D0_D7), .clk(not_4_out), .Q(register_2_q));  // open: en, clr
  not not_4 (not_4_out, or_1_out);
  or or_2 (or_2_out, or_6_out, or_3_out);
  assign out_12 = not_5_out ? register_2_q : 8'bz;  // Controlled_Buffer controlled_buffer_1
  not not_5 (not_5_out, or_5_out);
  or or_3 (or_3_out, WR, A1);
  and and_2 (and_2_out, d_ff_1_q, IEI);
  and and_3 (IEO, IEI, d_ff_1_qn);
  or or_4 (or_4_out, M1, IORQ);
  or or_5 (or_5_out, d_ff_1_qn, or_4_out);
  or or_6 (or_6_out, IORQ, Ax);
  or or_7 (or_7_out, WR, A0);
  not not_6 (INT, and_2_out);

  // Notes on the sheet:
  //   freq. divider
endmodule
