// Logisim project RAM512K.circ as structural Verilog: 1 circuit, main circuit main
module main (
  input  [13:0] A0_A13,
  input  MEMRQ,
  input  A15,
  input  A14,
  input  [7:0] in_5,
  input  A5,
  input  IORQ,
  input  WR,
  input  RD,
  output RAM_SEL_prime
);

  wire not_1_out, not_2_out, not_3_out, not_4_out, or_1_out, or_3_out, or_4_out;
  wire [4:0] controlled_buffer_1_out;
  wire [7:0] register_1_q;

  not not_1 (not_1_out, A15);
  not not_2 (not_2_out, A14);
  or or_1 (or_1_out, A5, IORQ);
  or or_2 (RAM_SEL_prime, MEMRQ, not_1_out);
  or or_3 (or_3_out, not_1_out, not_2_out);
  or or_4 (or_4_out, or_1_out, WR);
  not not_3 (not_3_out, or_4_out);
  Register register_1 (.D(in_5), .clk(not_3_out), .Q(register_1_q));  // open: en, clr
  not not_4 (not_4_out, or_3_out);
  assign controlled_buffer_1_out = not_4_out ? register_1_q[4:0] : 5'bz;  // Controlled_Buffer controlled_buffer_1
  Pull_Resistor pull_resistor_1 (.node(controlled_buffer_1_out));
  RAM #(.addrWidth(19), .\type ("nonvolatile")) ram_1 (
    .addr({controlled_buffer_1_out, A0_A13}), .we(WR), .oe(RD), .din(in_5));  // open: clk, dout

  // Other names for the same wires on the sheet: Data[7:0] = in_5

  // Notes on the sheet:
  //   D7-D0
  //   bankSwitchOut
  //   bankSwitchIn
endmodule
