// Logisim project RomBankSwitching.circ as structural Verilog: 1 circuit, main circuit main
module main (
  input  [13:0] in_1,
  input  A14,
  input  A15,
  input  MEMRQ,
  input  VRAMSEL_prime,
  input  [7:0] in_6,
  input  A5,
  input  IORQ,
  input  WR,
  output RAMSEL,
  output ROMSEL
);

  wire not_1_out, not_2_out, not_3_out, not_4_out, or_1_out, or_3_out, or_4_out;
  wire [7:0] pull_resistor_1_node, register_1_q;

  not not_1 (not_1_out, A14);
  not not_2 (not_2_out, A15);
  or or_1 (or_1_out, A5, IORQ);
  or or_2 (RAMSEL, not_2_out, MEMRQ);
  or or_3 (or_3_out, MEMRQ, A15);
  or or_4 (or_4_out, or_1_out, WR);
  or or_5 (ROMSEL, or_3_out, VRAMSEL_prime);
  Register register_1 (.D(in_6), .clk(not_3_out), .Q(register_1_q));  // open: en, clr
  not not_3 (not_3_out, or_4_out);
  not not_4 (not_4_out, not_1_out);
  Pull_Resistor pull_resistor_1 (.node(pull_resistor_1_node));
  assign pull_resistor_1_node = not_4_out ? register_1_q : 8'bz;  // Controlled_Buffer controlled_buffer_1
  ROM #(.addrWidth(17)) rom_1 (.addr({pull_resistor_1_node[2:0], in_1}));  // open: data
  RAM #(.addrWidth(19)) ram_1 (.addr({pull_resistor_1_node[7:3], in_1}));  // open: we, oe, clk, din, dout

  // Notes on the sheet:
  //   A0-A13
  //   D0-D7
  //   I may not need the WR signal
endmodule
