// Logisim project VGA.circ as structural Verilog: 1 circuit, main circuit main
module main (
  output VGA_out
);

  wire clock_1_out, counter_1_carry, nor_1_out;
  wire [1:0] undriven;
  wire [7:0] counter_1_q, ram_1_dout;
  wire [8:5] counter_2_q_2;
  wire [9:0] counter_2_q;

  Clock clock_1 (.out(clock_1_out));
  Counter counter_1 (.clk(clock_1_out), .carry(counter_1_carry), .Q(counter_1_q));  // open: clr, load, up, count, D
  RAM #(.addrWidth(11)) ram_1 (
    .addr({undriven, counter_2_q_2, counter_1_q[7:3]}), .dout(ram_1_dout));  // open: we, oe, clk, din
  nor nor_1 (nor_1_out, counter_1_q[0], counter_1_q[1], counter_1_q[2]);
  Counter #(.max('h3ff), .width(10)) counter_2 (
    .clk(counter_1_carry), .Q({counter_2_q[9], counter_2_q_2, counter_2_q[4:0]}));  // open: clr, load, up, count, D, carry
  // Shift_Register shift_register_1: pin names not known; wires that end beside it: nor_1_out, clock_1_out, VGA_out
  ROM #(.addrWidth(10)) rom_1 (.addr({ram_1_dout[6:0], counter_2_q[4:2]}));  // open: data

  // Notes on the sheet:
  //   X counter
  //   Image RAM
  //   Y counter
  //   Character ROM
endmodule
