// Logisim project VideoRAMSEL.circ as structural Verilog: 1 circuit, main circuit main
module main (
  input  A15,
  input  A14,
  input  A13,
  input  A12,
  input  A11,
  output To_ROMSEL,
  output Video_RAM_SEL
);

  wire not_1_out, not_2_out;

  not not_1 (not_1_out, A15);
  not not_2 (not_2_out, A14);
  and and_1 (To_ROMSEL, not_1_out, not_2_out, A13, A12, A11);
  not not_3 (Video_RAM_SEL, To_ROMSEL);
endmodule
