// Logisim project VideoRamAddressDecode.circ as structural Verilog: 1 circuit, main circuit main
module main (
  input  A10,
  input  A12,
  input  A13,
  input  A14,
  input  A15,
  output VRAMSEL_prime,
  output VRAMSEL
);

  wire and_1_out, and_2_out, and_3_out, not_1_out, not_2_out;

  not not_1 (not_1_out, A14);
  not not_2 (not_2_out, A15);
  and and_1 (and_1_out, A12, A13);
  and and_2 (and_2_out, not_1_out, not_2_out);
  and and_3 (and_3_out, and_1_out, and_2_out);
  and and_4 (VRAMSEL_prime, A10, and_3_out);
  not not_3 (VRAMSEL, VRAMSEL_prime);
endmodule
