// Logisim project AddressDecoding.circ as structural Verilog: 1 circuit, main circuit main
module main (
  input  A15_MEMRQ,
  input  WR,
  input  A14,
  input  Ax,
  input  IORQ__M1,
  output nVRAM,
  output PIXEL_WR,
  output COLOUR_WR,
  output SHIFT_WR
);

  wire not_1_out, or_1_out, or_2_out;

  or or_1 (or_1_out, A15_MEMRQ, WR);
  not not_1 (not_1_out, A14);
  or or_2 (or_2_out, Ax, IORQ__M1);
  or or_3 (PIXEL_WR, or_1_out, A14);
  or or_4 (COLOUR_WR, or_1_out, not_1_out);
  not not_2 (SHIFT_WR, or_2_out);
  not not_3 (nVRAM, or_1_out);
endmodule
