// Logisim project lcdDisplayAddressDecoding.circ as structural Verilog: 1 circuit, main circuit main
module main (
  input  IO,
  input  A3,
  input  WR,
  input  RD
);

  wire not_1_out, not_2_out, not_3_out, not_4_out, or_1_out, or_2_out, or_3_out;

  not not_1 (not_1_out, WR);
  not not_2 (not_2_out, RD);
  or or_1 (or_1_out, IO, A3);
  or or_2 (or_2_out, not_1_out, not_2_out);
  not not_3 (not_3_out, or_2_out);
  or or_3 (or_3_out, or_1_out, not_3_out);
  not not_4 (not_4_out, or_3_out);
  // Probe on not_4_out
endmodule
