// Logisim project memoryProtection.circ as structural Verilog: 1 circuit, main circuit main
module main (
  input  MEMRQ,
  input  WR,
  input  A14,
  input  A15,
  input  [14:0] A14_A0,
  input  [7:0] in_6,
  input  IORQ,
  input  A7,
  input  RD,
  output NMI
);

  wire not_1_out, not_2_out, or_1_out, or_2_out, or_3_out, or_4_out, or_6_out;
  wire [7:0] controlled_buffer_1_out, register_1_q;

  or or_1 (or_1_out, IORQ, A7);
  or or_2 (or_2_out, WR, or_1_out);
  not not_1 (not_1_out, or_2_out);
  Register register_1 (.D(in_6), .clk(not_1_out), .Q(register_1_q));  // open: en, clr
  or or_3 (or_3_out, MEMRQ, WR);
  or or_4 (or_4_out, A14, A15);
  not not_2 (not_2_out, or_4_out);
  assign controlled_buffer_1_out = A15 ? register_1_q : 8'bz;  // Controlled_Buffer controlled_buffer_1
  or or_5 (NMI, or_3_out, or_4_out);
  or or_6 (or_6_out, or_3_out, not_2_out);
  RAM #(.addrWidth(19), .\type ("nonvolatile")) ram_1 (
    .addr({controlled_buffer_1_out[3:0], A14_A0}), .we(or_6_out), .oe(RD), .din(in_6));  // open: clk, dout

  // Notes on the sheet:
  //   D7-D0
  //   Protects the first 16K of NVRAM from accidental writes
endmodule
